# Fritzing sketch PCB (saved by Fritzing 0.9.4)
circuit board: 7.13452cm x 7.90593cm
breadboards: 1

parts:
  U1 = NodeMCU V1.0
  Temp- = Momentary Switch [package=ksa_sealed_tac_switch]
  On/Off = Momentary Switch [package=ksa_sealed_tac_switch]
  Temp+ = Momentary Switch [package=ksa_sealed_tac_switch]
  R2 = Resistor [tolerance=±5% resistance=10k package=THT]
  R3 = Resistor [tolerance=±5% resistance=10k package=THT]
  R4 = Resistor [tolerance=±5% resistance=10k package=THT]
  JP1 = Header 3 [package=jst-3-pth]
  JP2 = Header 3 [package=jst-3-pth]

nets:
  N1: U1.D3, JP1.1
  N2: U1.D4, JP2.1
  N3: U1.3V3, Temp-.3, Temp-.4, On/Off.3, On/Off.4, Temp+.3, Temp+.4, JP1.2, JP2.2
  N4: U1.GND, R2.Pin_0, R3.Pin_0, R4.Pin_0, JP1.3, JP2.3
  N5: U1.D5, Temp+.1, Temp+.2, R4.Pin_1
  N6: U1.D6, Temp-.1, Temp-.2, R3.Pin_1
  N7: U1.D7, On/Off.1, On/Off.2, R2.Pin_1

custom parts:
  NodeMCU V1.0: ESP8266 based NodeMCU
